# Fritzing sketch Wiring (saved by Fritzing 0.9.3b)

parts:
  Part2 = Arduino Pro Mini v13
  Part3 = Bluetooth HC-05 Macho
  Composant2 = HC-SR501 Body Sensor Module

nets:
  N1: Part2.D0/TX, Part3.RXD
  VCC: Part2.VCC, Part3.VCC, Composant2.OUT
  GND: Part2.GND, Part3.GND, Composant2.GND
  N2: Part2.D5_PWM, Composant2.VCC

custom parts:
  HC-SR501 Body Sensor Module: Pyroelectric Infrared PIR Motion Sensor Detector Module
